// Logisim project mata3820171.circ as structural Verilog: 1 circuit, main circuit main
module main (
  input  [7:0] in_1,
  input  [1:0] in_2,
  input  [1:0] in_3,
  output [7:0] out_4,
  output [7:0] R1,
  output [7:0] R2,
  output [7:0] out_7,
  output [7:0] out_8,
  output [7:0] out_9,
  output [7:0] out_10,
  output [7:0] out_11,
  output [7:0] out_12,
  output [7:0] out_13,
  output [7:0] out_14,
  output [7:0] out_15,
  output [7:0] out_16,
  output [7:0] out_17,
  output [7:0] out_18,
  output [7:0] out_19,
  output [7:0] out_20,
  output [7:0] out_21,
  output [7:0] out_22,
  output [7:0] out_23,
  output [7:0] out_24,
  output [7:0] out_25,
  output [7:0] out_26,
  output [7:0] out_27,
  output [7:0] out_28,
  output [7:0] out_29,
  output [7:0] out_30,
  output [7:0] out_31,
  output [7:0] out_32,
  output [7:0] out_33,
  output [7:0] out_34,
  output [7:0] out_35,
  output [7:0] out_36,
  output [7:0] out_37,
  output [7:0] out_38,
  output [7:0] out_39,
  output [7:0] out_40,
  output [7:0] out_41,
  output [7:0] out_42,
  output [7:0] out_43,
  output [7:0] out_44,
  output [7:0] out_45
);

  wire clock_1_out, undriven;
  wire [7:0] multiplexer_1_out, multiplexer_2_out, undriven_2, undriven_3, undriven_4;

  Clock clock_1 (.out(clock_1_out));
  Register register_1 (.D(in_1), .en(undriven), .Q(out_4), .clk(clock_1_out));  // open: clr
  Multiplexer #(.select(2), .width(8)) multiplexer_1 (
    .in0(out_4), .in1(undriven_2), .in2(undriven_3), .in3(undriven_4), .out(multiplexer_1_out), .sel(in_2));  // open: en
  Register register_2 (.D(undriven_2), .Q(R1), .clk(clock_1_out));  // open: en, clr
  Register register_3 (.D(undriven_3), .Q(R2), .clk(clock_1_out));  // open: en, clr
  Multiplexer #(.select(2), .width(8)) multiplexer_2 (
    .in0(out_4), .in1(undriven_2), .in2(undriven_3), .in3(undriven_4), .out(multiplexer_2_out), .sel(in_3));  // open: en
  Register register_4 (.D(undriven_4), .Q(out_7), .clk(clock_1_out));  // open: en, clr
  Demultiplexer #(.select(4), .width(8)) demultiplexer_1 (
    .out0(out_9), .out1(out_10), .out2(out_12), .out3(out_13), .out4(out_14), .out5(out_16), .out6(out_17),
    .out7(out_19), .out8(out_20), .out9(out_21), .out10(out_23), .out11(out_24), .out12(out_25),
    .out13(out_27), .out14(out_28), .out15(out_29), .in(multiplexer_2_out), .sel(4'b0001));  // open: en
  Demultiplexer #(.select(4), .width(8)) demultiplexer_2 (
    .out0(out_30), .out1(out_31), .out2(out_32), .out3(out_33), .out4(out_34), .out5(out_35), .out6(out_36),
    .out7(out_37), .out8(out_38), .out9(out_39), .out10(out_40), .out11(out_41), .out12(out_42),
    .out13(out_43), .out14(out_44), .out15(out_45), .in(multiplexer_1_out), .sel(4'b0001));  // open: en
  assign out_8 = out_9 & out_30;  // AND_Gate and_1, 8 bits wide
  assign out_11 = out_10 | out_31;  // OR_Gate or_1, 8 bits wide
  assign out_15 = out_12 ^ out_32;  // XOR_Gate xor_1, 8 bits wide
  assign out_18 = ~out_13;  // NOT_Gate not_1, 8 bits wide
  Adder adder_1 (.a(out_14), .b(out_34), .out(out_22));  // open: cin, cout
  Subtractor subtractor_1 (.a(out_16), .b(out_35), .out(out_26));  // open: bin, bout

  // Notes on the sheet:
  //   R0
  //   R3
endmodule
